# Fritzing sketch fritzingSchematic (saved by Fritzing 0.9.6b)
breadboards: 1

parts:
  BeagleBone1 = BeagleBone Black
  T1 = LM35 Temperature Sensor [package="TO92 [THT]"]

nets:
  N1: BeagleBone1.P9_2_-_GND, T1.GND
  N2: BeagleBone1.P9_3_-_3.3V, T1.+Vs
  N3: BeagleBone1.P9_39_-_AIN0, T1.Vout

custom parts:
  BeagleBone Black: BeagleBone Black rev. A5B
